# Fritzing sketch BLE_Motor_Control (saved by Fritzing 0.9.9b)

parts:
  Part1 = Arduino Uno (Rev3)
  R1 = Rotary Potentiometer (Small) [maximum_resistance=10kΩ package=THT]

nets:
  N1: Part1.A0, R1.wiper
  N2: Part1.3V3, R1.leg2
  N3: Part1.GND, R1.leg1
